// Digital circuit ALU.dig as structural Verilog
module ALU (
);

  wire binary_xor_1_p3, binary_xor_1_p4, comparator_1_eq, comparator_2_eq, comparator_3_eq, comparator_4_eq,
       comparator_5_eq, comparator_6_eq, comparator_7_eq, comparator_8_eq, comparator_9_eq, comparator_10_eq,
       comparator_11_eq, comparator_12_eq, comparator_13_eq, comparator_14_eq, comparator_15_eq,
       comparator_16_eq, comparator_17_eq, comparator_18_eq;
  wire [7:0] adder_subtractor_1_q, binary_xor_1_p1, binary_xor_1_p2, binary_xor_1_p5, undriven;
  wire [7:1] undriven_2, undriven_3, undriven_4, undriven_5, undriven_6, undriven_7, undriven_8, undriven_9,
       undriven_10, undriven_11, undriven_12, undriven_13, undriven_14, undriven_15, undriven_16,
       undriven_17, undriven_18, undriven_19;

  Comparator #(.Bits(8)) comparator_1 (.a(undriven), .b({undriven_2, 1'b1}), .eq(comparator_1_eq));  // open: gt, lt
  Comparator #(.Bits(8)) comparator_2 (.a(undriven), .b({undriven_3, 1'b1}), .eq(comparator_2_eq));  // open: gt, lt
  Comparator #(.Bits(8)) comparator_3 (.a(undriven), .b({undriven_4, 1'b1}), .eq(comparator_3_eq));  // open: gt, lt
  Comparator #(.Bits(8)) comparator_4 (.a(undriven), .b({undriven_5, 1'b1}), .eq(comparator_4_eq));  // open: gt, lt
  Comparator #(.Bits(8)) comparator_5 (.a(undriven), .b({undriven_6, 1'b1}), .eq(comparator_5_eq));  // open: gt, lt
  Comparator #(.Bits(8)) comparator_6 (.a(undriven), .b({undriven_7, 1'b1}), .eq(comparator_6_eq));  // open: gt, lt
  Comparator #(.Bits(8)) comparator_7 (.a(undriven), .b({undriven_8, 1'b1}), .eq(comparator_7_eq));  // open: gt, lt
  Comparator #(.Bits(8)) comparator_8 (.a(undriven), .b({undriven_9, 1'b1}), .eq(comparator_8_eq));  // open: gt, lt
  Comparator #(.Bits(8)) comparator_9 (.a(undriven), .b({undriven_10, 1'b1}), .eq(comparator_9_eq));  // open: gt, lt
  Comparator #(.Bits(8)) comparator_10 (.a(undriven), .b({undriven_11, 1'b1}), .eq(comparator_10_eq));  // open: gt, lt
  Comparator #(.Bits(8)) comparator_11 (.a(undriven), .b({undriven_12, 1'b1}), .eq(comparator_11_eq));  // open: gt, lt
  Comparator #(.Bits(8)) comparator_12 (.a(undriven), .b({undriven_13, 1'b1}), .eq(comparator_12_eq));  // open: gt, lt
  Comparator #(.Bits(8)) comparator_13 (.a(undriven), .b({undriven_14, 1'b1}), .eq(comparator_13_eq));  // open: gt, lt
  Comparator #(.Bits(8)) comparator_14 (.a(undriven), .b({undriven_15, 1'b1}), .eq(comparator_14_eq));  // open: gt, lt
  Comparator #(.Bits(8)) comparator_15 (.a(undriven), .b({undriven_16, 1'b1}), .eq(comparator_15_eq));  // open: gt, lt
  Comparator #(.Bits(8)) comparator_16 (.a(undriven), .b({undriven_17, 1'b1}), .eq(comparator_16_eq));  // open: gt, lt
  Comparator #(.Bits(8)) comparator_17 (.a(undriven), .b({undriven_18, 1'b1}), .eq(comparator_17_eq));  // open: gt, lt
  Comparator #(.Bits(8)) comparator_18 (.a(undriven), .b({undriven_19, 1'b1}), .eq(comparator_18_eq));  // open: gt, lt
  Adder_Subtractor adder_subtractor_1 (
    .A(binary_xor_1_p5), .B(binary_xor_1_p1), .ADD(comparator_1_eq), .ADC(comparator_2_eq),
    .SUB(comparator_3_eq), .CLK(binary_xor_1_p4), .Q(adder_subtractor_1_q));  // open: C_in, C_8, F, STC, STF
  Incrementor incrementor_1 (
    .C(binary_xor_1_p2), .INC(comparator_4_eq), .DEC(comparator_5_eq), .CLK(binary_xor_1_p4),
    .Q(adder_subtractor_1_q));  // open: C_8, F, STC, STF, Q_S
  Comparator comparator_19 (
    .A(binary_xor_1_p5), .B(binary_xor_1_p1), .CMP_bigger(comparator_6_eq), .CMP_equal(comparator_7_eq),
    .CMP_smaller(comparator_8_eq), .CLK(binary_xor_1_p4), .Q(adder_subtractor_1_q));
  Shift_Register shift_register_1 (
    .A(binary_xor_1_p5), .STR(binary_xor_1_p3), .SHR(comparator_9_eq), .SHL(comparator_10_eq),
    .CLK(binary_xor_1_p4));  // open: Q
  Bitwise_NOT bitwise_not_1 (
    .A(binary_xor_1_p5), .EN(comparator_11_eq), .CLK(binary_xor_1_p4), .Q(adder_subtractor_1_q));
  Bitwise_OR bitwise_or_1 (
    .A(binary_xor_1_p5), .B(binary_xor_1_p1), .EN(comparator_12_eq), .CLK(binary_xor_1_p4));  // open: Q
  Bitwise_AND bitwise_and_1 (
    .A(binary_xor_1_p5), .B(binary_xor_1_p1), .EN(comparator_13_eq), .CLK(binary_xor_1_p4),
    .Q(adder_subtractor_1_q));
  Bitwise_XOR bitwise_xor_1 (
    .A(binary_xor_1_p5), .B(binary_xor_1_p1), .EN(comparator_14_eq), .CLK(binary_xor_1_p4),
    .Q(adder_subtractor_1_q));
  Binary_NOT binary_not_1 (
    .A(binary_xor_1_p5[0]), .EN(comparator_15_eq), .CLK(binary_xor_1_p4), .Q(adder_subtractor_1_q));
  Binary_OR binary_or_1 (
    .A(binary_xor_1_p5[0]), .B(binary_xor_1_p1[0]), .EN(comparator_16_eq), .CLK(binary_xor_1_p4),
    .Q(adder_subtractor_1_q));
  Binary_AND binary_and_1 (
    .A(binary_xor_1_p5[0]), .B(binary_xor_1_p1[0]), .EN(comparator_17_eq), .CLK(binary_xor_1_p4),
    .Q(adder_subtractor_1_q));
  // Binary_XOR binary_xor_1: pin names not known; wires that end beside it: binary_xor_1_p1, binary_xor_1_p2, binary_xor_1_p3, binary_xor_1_p4, binary_xor_1_p5, binary_xor_1_p1, comparator_18_eq, binary_xor_1_p4, adder_subtractor_1_q, adder_subtractor_1_q
  // Pins of 1 and 8 bits meet at binary_xor_1_p5
  // Pins of 1 and 8 bits meet at binary_xor_1_p1
  // Pins of 1 and 8 bits meet at {undriven_2, 1'b1}
  // Pins of 1 and 8 bits meet at {undriven_3, 1'b1}
  // Pins of 1 and 8 bits meet at {undriven_4, 1'b1}
  // Pins of 1 and 8 bits meet at {undriven_7, 1'b1}
  // Pins of 1 and 8 bits meet at {undriven_8, 1'b1}
  // Pins of 1 and 8 bits meet at {undriven_9, 1'b1}
  // Pins of 1 and 8 bits meet at {undriven_12, 1'b1}
  // Pins of 1 and 8 bits meet at {undriven_13, 1'b1}
  // Pins of 1 and 8 bits meet at {undriven_14, 1'b1}
  // Pins of 1 and 8 bits meet at {undriven_15, 1'b1}

  // Notes on the sheet:
  //   CMD
  //   A
  //   B
  //   C
  //   DAT
  //   CLK
  //   Q
endmodule
