// Digital circuit CPU.dig as structural Verilog
module CPU (
  input  clk,
  input  CLR_PC
);

  wire comparator_1_eq, comparator_2_eq, comparator_3_eq, comparator_4_eq, comparator_5_eq, comparator_6_eq,
       comparator_7_eq, comparator_8_eq, comparator_9_eq, comparator_10_eq, comparator_11_eq;
  wire [7:0] flash_memory_1_q_cmd, flash_memory_1_q_dat, rom_1_d, rom_2_d;
  wire [15:0] flash_memory_1_q_adr, programme_counter_1_ln, rom_3_d;

  Comparator #(.Bits(8)) comparator_1 (.a(flash_memory_1_q_cmd), .b(8'h1), .eq(comparator_1_eq));  // open: gt, lt
  Comparator #(.Bits(8)) comparator_2 (.a(flash_memory_1_q_cmd), .b(8'h2), .eq(comparator_2_eq));  // open: gt, lt
  Comparator #(.Bits(8)) comparator_3 (.a(flash_memory_1_q_cmd), .b(8'h3), .eq(comparator_3_eq));  // open: gt, lt
  Comparator #(.Bits(8)) comparator_4 (.a(flash_memory_1_q_cmd), .b(8'h4), .eq(comparator_4_eq));  // open: gt, lt
  Comparator #(.Bits(8)) comparator_5 (.a(flash_memory_1_q_cmd), .b(8'h5), .eq(comparator_5_eq));  // open: gt, lt
  Comparator #(.Bits(8)) comparator_6 (.a(flash_memory_1_q_cmd), .b(8'h6), .eq(comparator_6_eq));  // open: gt, lt
  Comparator #(.Bits(8)) comparator_7 (.a(flash_memory_1_q_cmd), .b(8'h7), .eq(comparator_7_eq));  // open: gt, lt
  Comparator #(.Bits(8)) comparator_8 (.a(flash_memory_1_q_cmd), .b(8'h8), .eq(comparator_8_eq));  // open: gt, lt
  Comparator #(.Bits(8)) comparator_9 (.a(flash_memory_1_q_cmd), .b(8'h9), .eq(comparator_9_eq));  // open: gt, lt
  Comparator #(.Bits(8)) comparator_10 (.a(flash_memory_1_q_cmd), .b(8'ha), .eq(comparator_10_eq));  // open: gt, lt
  Comparator #(.Bits(8)) comparator_11 (.a(flash_memory_1_q_cmd), .b(8'hb), .eq(comparator_11_eq));  // open: gt, lt
  ROM #(.AddrBits(16), .Bits(8)) rom_1 (.A(programme_counter_1_ln), .sel(1'b1), .D(rom_1_d));
  ROM #(.AddrBits(16), .Bits(8)) rom_2 (.A(programme_counter_1_ln), .sel(1'b1), .D(rom_2_d));
  ROM #(.AddrBits(16), .Bits(16)) rom_3 (.A(programme_counter_1_ln), .sel(1'b1), .D(rom_3_d));
  Programme_Counter programme_counter_1 (
    .DAT(flash_memory_1_q_dat), .ADR(flash_memory_1_q_adr), .CLK(clk), .JMP(comparator_1_eq),
    .CJP(comparator_2_eq), .CLR(CLR_PC), .LN(programme_counter_1_ln));
  Flash_Memory flash_memory_1 (
    .CMD(rom_1_d), .DAT(rom_2_d), .ADR(rom_3_d), .CLK(clk), .Q_CMD(flash_memory_1_q_cmd),
    .Q_DAT(flash_memory_1_q_dat), .Q_ADR(flash_memory_1_q_adr));
  ALU alu_1 (.CMD(flash_memory_1_q_cmd), .DAT(flash_memory_1_q_dat), .CLK(clk), .Q(flash_memory_1_q_dat));
  RAM ram_1 (
    .DAT(flash_memory_1_q_dat), .ADR(flash_memory_1_q_adr), .STR_reg1(comparator_3_eq),
    .STR_reg2(comparator_4_eq), .STR(comparator_5_eq), .LD(comparator_6_eq), .STR_todata(comparator_7_eq),
    .LD_fromdata(comparator_8_eq), .LD_reg1(comparator_9_eq), .LD_reg2(comparator_10_eq),
    .LD_toaddrbus(comparator_11_eq), .CLK(clk), .Q_DAT(flash_memory_1_q_dat), .Q_ADR(flash_memory_1_q_adr));

  // Notes on the sheet:
  //   clk: Hz: 5
  //   LN
  //   CMD
  //   LN: output from the programmme counter,
  //   the current line of code being executed
  //   DAT
  //   ADR
  //   CLK
  //   - Flash memory
  //   contents of rom_1 (hex, n*v repeats v):
  //   27
endmodule
